# Fritzing sketch Robot_schema (saved by Fritzing 0.9.3b)
breadboards: 1

parts:
  Part1 = Arduino Mega 2560 (Rev3)
  J1 = Basic Servo

nets:
  GND: Part1.GND, J1.gnd
  5V: Part1.5V, J1.vcc
  N1: Part1.D3_PWM, J1.pulse
